# Fritzing sketch arduTram (saved by Fritzing 0.7.12b)
breadboards: 1

parts:
  DC_Power1 = DC Power [voltage=5]
  Arduino_Ethernet_Shield1 = Arduino Ethernet Shield
  M1 = DC Motor
  L1 = Solenoid
  IC1 = H-Bridge [package=THT]
  R1 = Photocell (LDR) [package=THT]
  R2 = Photocell (LDR) [package=THT]
  IC2 = H-Bridge [package=THT]
  L2 = Solenoid
  LED1 = LED - 5mm [color="Red (633nm)" package="5 mm [THT]"]
  LED2 = LED - 5mm [color="Red (633nm)" package="5 mm [THT]"]
  R5 = Resistor [tolerance=±5% resistance=10k package=THT]
  R6 = Resistor [tolerance=±5% resistance=10k package=THT]

nets:
  N1: DC_Power1.V+, IC1.VCC2, IC2.VCC2
  GND: DC_Power1.GND, Arduino_Ethernet_Shield1.GND, IC1.1_2EN, IC1.GND1, IC1.GND2, IC1.GND3, IC1.GND4, IC2.GND1, IC2.GND2, IC2.GND3, IC2.GND4, LED1.cathode, R5.Pin_1, R6.Pin_1
  N2: Arduino_Ethernet_Shield1.D9, IC1.4A
  N3: Arduino_Ethernet_Shield1.D8, IC2.4A
  N4: Arduino_Ethernet_Shield1.D7, IC2.3A
  N5: Arduino_Ethernet_Shield1.D6, IC2.1A
  N6: Arduino_Ethernet_Shield1.D5, IC2.2A
  N7: Arduino_Ethernet_Shield1.D3, IC1.3A
  N8: Arduino_Ethernet_Shield1.+5V, IC1.3_4EN, IC1.VCC1, R1.pin_0, R2.pin_0, IC2.1_2EN, IC2.3_4EN, IC2.VCC1
  N9: Arduino_Ethernet_Shield1.A0, R2.pin_1, R6.Pin_0
  N10: Arduino_Ethernet_Shield1.A1, R1.pin_1, R5.Pin_0
  N11: M1.pin_1, IC1.4Y
  N12: M1.pin_2, IC1.3Y
  N13: L1.pin1, IC2.3Y
  N14: L1.pin2, IC2.4Y
  N15: IC2.2Y, L2.pin1
  N16: LED1.anode, LED2.cathode
